# Fritzing sketch MIDI IO circuit (saved by Fritzing 0.9.2b)
breadboards: 1

parts:
  DIN1 = DIN-5 jack (MIDI) [package=THT]
  DIN2 = DIN-5 jack (MIDI) [package=THT]
  U1 = OPTO_DARL_6N138S [package=8-smd]
  R1 = Resistor [tolerance=±5% resistance=220 package="0805 [SMD]"]
  R2 = Resistor [tolerance=±5% resistance=220 package="0805 [SMD]"]
  R3 = Resistor [tolerance=±5% resistance=220 package="0805 [SMD]"]
  R4 = Resistor [tolerance=±5% resistance=10k package="0805 [SMD]"]
  D1 = Diode [package=diode-1n4148]
  R5 = Resistor [tolerance=±5% resistance=220 package="0805 [SMD]"]
  R6 = Resistor [tolerance=±5% resistance=220 package="0805 [SMD]"]

nets:
  N1: DIN1.5, R3.Pin_0
  N2: DIN1.4, U1.C, D1.A
  N3: DIN2.5, R6.Pin_0
  N4: DIN2.2, U1.GND, R4.Pin_1
  N5: DIN2.4, R5.Pin_0
  N6: U1.A, R3.Pin_1, D1.C
  N7: U1.VOUT, R1.Pin_1
  N8: U1.VCC, R2.Pin_1, R5.Pin_1
  N9: R1.Pin_0, R2.Pin_0

notes:
  Front of MIDI-in socket
  To a BBB serial RX pin
  To BBB power and ground
  To a BBB serial TX pin
  Front of MIDI-out socket
