# Fritzing sketch panel circuit (saved by Fritzing 0.9.2b)
breadboards: 1

parts:
  Part1 = Arduino Pro Mini v13
  U1 = 74HC4067 [package=ssop24]
  U2 = 74HC4067 [package=ssop24]
  U3 = 74HC4067 [package=ssop24]
  R1 = Rotary Potentiometer (Large) [maximum_resistance=100kΩ package=THT]
  C1 = Ceramic Capacitor [capacitance=1pF package="1206 [SMD, multilayer]"]
  C2 = Ceramic Capacitor [capacitance="100 nF" package="1206 [SMD, multilayer]"]
  C3 = Ceramic Capacitor [capacitance="100 nF" package="1206 [SMD, multilayer]"]
  C4 = Ceramic Capacitor [capacitance="100 nF" package="1206 [SMD, multilayer]"]

nets:
  GND: Part1.GND, U1.GND, U1.EN, U2.GND, U2.EN, U3.GND, U3.EN, R1.leg1, C1.0, C2.0, C3.0, C4.0
  VCC: Part1.VCC, U1.VCC, U2.VCC, U3.VCC, R1.leg2, C1.1, C2.1, C3.1, C4.1
  N1: Part1.A2, U3.COM
  N2: Part1.A1, U2.COM
  N3: Part1.A0, U1.COM
  N4: Part1.D13/SCK, U3.S3
  N5: Part1.D12/MISO, U3.S2
  N6: Part1.D11_PWM/MOSI, U3.S1
  N7: Part1.D10_PWM/SS, U3.S0
  N8: Part1.D9_PWM, U2.S3
  N9: Part1.D8, U2.S2
  N10: Part1.D7, U2.S1
  N11: Part1.D6_PWM, U2.S0
  N12: Part1.D5_PWM, U1.S3
  N13: Part1.D4, U1.S2
  N14: Part1.D3_PWM, U1.S1
  N15: Part1.D2, U1.S0
  N16: U1.CHAN11, R1.wiper

notes:
  Serial RX/TX to BBB
  Power/ground to BBB
