# Fritzing sketch key mech circuit v2 (saved by Fritzing 0.9.2b)
breadboards: 3

parts:
  J1 = Basic Force Sensing Resistor (FSR) [package=THT]
  J2 = Basic Force Sensing Resistor (FSR) [package=THT]
  J3 = Basic Force Sensing Resistor (FSR) [package=THT]
  J4 = Basic Force Sensing Resistor (FSR) [package=THT]
  J5 = Basic Force Sensing Resistor (FSR) [package=THT]
  J6 = Basic Force Sensing Resistor (FSR) [package=THT]
  J7 = Basic Force Sensing Resistor (FSR) [package=THT]
  J8 = Basic Force Sensing Resistor (FSR) [package=THT]
  U1 = 74HC4051 [package=so16]
  R1 = Resistor [tolerance=±5% resistance=10k package="1206 [SMD]"]
  R2 = Resistor [tolerance=±5% resistance=10k package="1206 [SMD]"]
  R3 = Resistor [tolerance=±5% resistance=10k package="1206 [SMD]"]
  R4 = Resistor [tolerance=±5% resistance=10k package="1206 [SMD]"]
  R5 = Resistor [tolerance=±5% resistance=10k package="1206 [SMD]"]
  R6 = Resistor [tolerance=±5% resistance=10k package="1206 [SMD]"]
  R7 = Resistor [tolerance=±5% resistance=10k package="1206 [SMD]"]
  R8 = Resistor [tolerance=±5% resistance=10k package="1206 [SMD]"]
  J9 = Basic Force Sensing Resistor (FSR) [package=THT]
  J10 = Basic Force Sensing Resistor (FSR) [package=THT]
  J11 = Basic Force Sensing Resistor (FSR) [package=THT]
  J12 = Basic Force Sensing Resistor (FSR) [package=THT]
  J13 = Basic Force Sensing Resistor (FSR) [package=THT]
  J14 = Basic Force Sensing Resistor (FSR) [package=THT]
  J15 = Basic Force Sensing Resistor (FSR) [package=THT]
  J16 = Basic Force Sensing Resistor (FSR) [package=THT]
  U2 = 74HC4051 [package=so16]
  R9 = Resistor [tolerance=±5% resistance=10k package="1206 [SMD]"]
  R10 = Resistor [tolerance=±5% resistance=10k package="1206 [SMD]"]
  R11 = Resistor [tolerance=±5% resistance=10k package="1206 [SMD]"]
  R12 = Resistor [tolerance=±5% resistance=10k package="1206 [SMD]"]
  R13 = Resistor [tolerance=±5% resistance=10k package="1206 [SMD]"]
  R14 = Resistor [tolerance=±5% resistance=10k package="1206 [SMD]"]
  R15 = Resistor [tolerance=±5% resistance=10k package="1206 [SMD]"]
  R16 = Resistor [tolerance=±5% resistance=10k package="1206 [SMD]"]
  J17 = Basic Force Sensing Resistor (FSR) [package=THT]
  J18 = Basic Force Sensing Resistor (FSR) [package=THT]
  Part1 = Arduino Pro Mini v13
  R17 = Resistor [tolerance=±5% resistance=10k package="1206 [SMD]"]
  R18 = Resistor [tolerance=±5% resistance=10k package="1206 [SMD]"]

nets:
  N1: J1.pin_0, U1.IO0, R1.Pin_0
  VDD: J1.pin_1, J2.pin_1, J3.pin_1, J4.pin_1, J5.pin_1, J6.pin_1, J7.pin_1, J8.pin_1, U1.VDD, J9.pin_1, J10.pin_1, J11.pin_1, J12.pin_1, J13.pin_1, J14.pin_1, J15.pin_1, J16.pin_1, U2.VDD, J17.pin_1, J18.pin_1, Part1.VCC
  N2: J2.pin_0, U1.IO1, R2.Pin_0
  N3: J3.pin_0, U1.IO2, R3.Pin_0
  N4: J4.pin_0, U1.IO3, R4.Pin_0
  N5: J5.pin_0, U1.IO4, R5.Pin_0
  N6: J6.pin_0, U1.IO5, R6.Pin_0
  N7: J7.pin_0, U1.IO6, R7.Pin_0
  N8: J8.pin_0, U1.IO7, R8.Pin_0
  N9: U1.IO, Part1.A0
  VSS: U1.INH, U1.VEE, U1.VSS, R1.Pin_1, R2.Pin_1, R3.Pin_1, R4.Pin_1, R5.Pin_1, R6.Pin_1, R7.Pin_1, R8.Pin_1, U2.INH, U2.VEE, U2.VSS, R9.Pin_1, R10.Pin_1, R11.Pin_1, R12.Pin_1, R13.Pin_1, R14.Pin_1, R15.Pin_1, R16.Pin_1, Part1.GND, R17.Pin_0, R18.Pin_0
  N10: U1.C, Part1.D4
  N11: U1.B, Part1.D3_PWM
  N12: U1.A, Part1.D2
  N13: J9.pin_0, U2.IO7, R9.Pin_0
  N14: J10.pin_0, U2.IO6, R10.Pin_0
  N15: J11.pin_0, U2.IO5, R11.Pin_0
  N16: J12.pin_0, U2.IO4, R12.Pin_0
  N17: J13.pin_0, U2.IO3, R13.Pin_0
  N18: J14.pin_0, U2.IO2, R14.Pin_0
  N19: J15.pin_0, U2.IO1, R15.Pin_0
  N20: J16.pin_0, U2.IO0, R16.Pin_0
  N21: U2.IO, Part1.A3
  N22: U2.C, Part1.D7
  N23: U2.B, Part1.D6_PWM
  N24: U2.A, Part1.D5_PWM
  N25: J17.pin_0, Part1.A1, R17.Pin_1
  N26: J18.pin_0, Part1.A2, R18.Pin_1
